# Fritzing sketch Simon Says (saved by Fritzing 1.0.4)
breadboards: 1

parts:
  Mod1 = Raspberry Pi Pico W
  U1 = WS2812 RGB LED matrix 1x8
  S1 = Pushbutton [package="[THT]"]
  S2 = Pushbutton [package="[THT]"]
  S3 = Pushbutton [package="[THT]"]
  S4 = Pushbutton [package="[THT]"]

nets:
  N1: Mod1.pin_1, U1.DIN
  N2: Mod1.pin_3, Mod1.pin_8, Mod1.pin_13, Mod1.pin_18, Mod1.pin_23, Mod1.pin_28, Mod1.pin_33, Mod1.pin_38, U1.GND, S1.Pin_1, S1.Pin_2, S2.Pin_1, S2.Pin_2, S3.Pin_1, S3.Pin_2, S4.Pin_1, S4.Pin_2
  N3: Mod1.pin_10, S3.Pin_3, S3.Pin_4
  N4: Mod1.pin_19, S4.Pin_3, S4.Pin_4
  N5: Mod1.pin_25, S2.Pin_3, S2.Pin_4
  N6: Mod1.pin_29, S1.Pin_3, S1.Pin_4
  N7: Mod1.pin_40, U1.VCC

custom parts:
  Raspberry Pi Pico W: Raspberry Pi Pico W. Based around the RP2040 microcontroller the Pico W is a low cost microcontroller device bringing Raspberry Pi quality, cost, and easy of use to the microcontroller space. The areas marked KEEPOUT in pcb silkscreen should not have traces running through them to avoid shorts on a soldered in module!
  WS2812 RGB LED matrix 1x8: WS2812 matrix 1x8
